// Logisim project 120811_2022_3.circ as structural Verilog: 1 circuit, main circuit main
module main (
  input  X,
  input  RES,
  output Y
);

  wire _1_out, _2_out, _3_out, _4_out, _5_out, _6_out, _7_out, _8_out, _9_out, _10_out, clock_1_out, J1_out,
       J2_out, J3_out, K1_out, K2_out, K3_out, nand_1_out, Z1_q, Z1_qn, Z2_q, Z2_qn, Z3_q, Z3_qn;

  nand nand_1 (nand_1_out, X, X);
  Clock clock_1 (.out(clock_1_out));
  nand _1 (_1_out, nand_1_out, Z1_qn, Z3_qn);
  nand _2 (_2_out, Z2_qn, Z3_qn);
  nand _3 (_3_out, X, Z2_q, Z3_q);
  nand _4 (_4_out, nand_1_out, Z1_q);
  nand _5 (_5_out, nand_1_out, Z2_qn, Z3_qn);
  nand _6 (_6_out, nand_1_out, Z1_q, Z3_q);
  nand _7 (_7_out, nand_1_out, Z1_q, Z2_q);
  nand _8 (_8_out, X, Z1_qn, Z2_qn);
  nand _9 (_9_out, Z3_q, Z1_q);
  nand _10 (_10_out, Z2_qn, Z3_q, X);
  nand J1 (J1_out, _1_out, _2_out, _3_out);
  nand K1 (K1_out, _4_out, Z3_q);
  nand J2 (J2_out, _4_out, _5_out);
  nand K2 (K2_out, _1_out, _6_out);
  nand J3 (J3_out, _7_out, _8_out);
  nand K3 (K3_out, _9_out, _9_out);
  nand nand_2 (Y, _10_out, _10_out);
  J_K_Flip_Flop Z1 (.J(J1_out), .clk(clock_1_out), .K(K1_out), .Q(Z1_q), .Qn(Z1_qn), .reset(RES));  // open: preset, en
  J_K_Flip_Flop Z2 (.J(J2_out), .clk(clock_1_out), .K(K2_out), .Q(Z2_q), .Qn(Z2_qn), .reset(RES));  // open: preset, en
  J_K_Flip_Flop Z3 (.J(J3_out), .clk(clock_1_out), .K(K3_out), .Q(Z3_q), .Qn(Z3_qn), .reset(RES));  // open: preset, en
endmodule
