// Logisim project 120811_zadanie 2.circ as structural Verilog: 1 circuit, main circuit main
module main (
  input  C,
  input  D,
  input  A,
  input  B,
  output A_DNF,
  output B_DNF,
  output C_DNF,
  output D_DNF,
  output E_DNF,
  output A_KNF,
  output B_KNF,
  output C_KNF,
  output D_KNF,
  output E_DNF_2
);

  wire A_out, B_out, C_out, D_out, n_A_nB_out, n_A_nC_nD_out, n_B_C_D_out, n_B_C_nD_2_out, n_B_C_nD_out,
       n_B_nC_D_out, n_nA_B_2_out, n_nA_B_out, n_nA_C_D_out, n_nB_C_nD_out, n_nB_nC_D_out, n_nB_nC_nD_out,
       nand_1_out, nand_2_out, nand_3_out, nand_4_out, nor_1_out, nor_2_out, nor_3_out, nor_4_out, nor_5_out,
       nor_6_out, nor_7_out, nor_8_out, nor_9_out, nor_10_out;

  not nand_1 (nand_1_out, A);  // NAND_Gate
  not u_A (A_out, A);  // NOR_Gate
  not nand_2 (nand_2_out, B);  // NAND_Gate
  not u_B (B_out, B);  // NOR_Gate
  not nand_3 (nand_3_out, C);  // NAND_Gate
  not u_C (C_out, C);  // NOR_Gate
  not nand_4 (nand_4_out, D);  // NAND_Gate
  nand n_B_C_nD (n_B_C_nD_out, B, C, nand_4_out);
  not u_D (D_out, D);  // NOR_Gate
  nand n_B_C_D (n_B_C_D_out, B, C, D);
  nand n_B_C_nD_2 (n_B_C_nD_2_out, B, B, C, nand_4_out);
  nand n_B_nC_D (n_B_nC_D_out, B, nand_3_out, D);
  nand n_A_nC_nD (n_A_nC_nD_out, A, nand_3_out, nand_4_out);
  nand n_nA_C_D (n_nA_C_D_out, nand_1_out, C, D);
  nand n_nA_B (n_nA_B_out, nand_1_out, B);
  nand n_A_nB (n_A_nB_out, A, A, nand_2_out);
  nand n_nB_C_nD (n_nB_C_nD_out, nand_2_out, C, C, nand_4_out);
  nand n_nB_nC_D (n_nB_nC_D_out, nand_2_out, nand_3_out, D);
  nand n_nB_nC_nD (n_nB_nC_nD_out, nand_2_out, nand_3_out, nand_4_out);
  nor n_nA_B_2 (n_nA_B_2_out, A_out, B);
  nor nor_1 (nor_1_out, A_out, C);
  nor nor_2 (nor_2_out, C_out, D);
  nor nor_3 (nor_3_out, A, B, C);
  nor nor_4 (nor_4_out, D_out, B_out);
  nor nor_5 (nor_5_out, A, D_out, C_out);
  nor nor_6 (nor_6_out, D, C, A);
  nor nor_7 (nor_7_out, A_out, C_out);
  nor nor_8 (nor_8_out, A_out, D);
  nor nor_9 (nor_9_out, D_out, A, B);
  nor nor_10 (nor_10_out, B_out, A);
  nand B_2 (B_DNF, n_B_C_D_out, n_nA_C_D_out, n_nA_B_out, n_A_nB_out);
  nand C_2 (C_DNF, n_B_C_nD_out, n_nB_C_nD_out, n_nB_nC_D_out, n_A_nB_out);
  nand D_2 (D_DNF, n_B_nC_D_out, n_nB_C_nD_out, n_nB_nC_nD_out, n_nA_B_out);
  nand E (E_DNF, n_nB_nC_nD_out, n_nA_C_D_out, n_nB_nC_D_out, n_A_nC_nD_out);
  nor A_2 (A_KNF, A_out, n_nA_B_2_out);
  nor B_3 (B_KNF, nor_1_out, nor_2_out, nor_3_out);
  nor nor_11 (C_KNF, nor_4_out, nor_5_out, nor_1_out, nor_6_out);
  nor D_3 (D_KNF, nor_7_out, nor_8_out, nor_9_out);
  nor nor_12 (E_DNF_2, n_nA_B_2_out, nor_2_out, nor_4_out, nor_10_out);
  nand A_3 (A_DNF, n_B_C_D_out, n_B_C_nD_2_out, n_B_nC_D_out, n_A_nC_nD_out);
endmodule
